// Logisim project lab6.1.circ as structural Verilog: 1 circuit, main circuit 控制器
module \控制器  (
  input  [6:0] opcode,
  input  [2:0] funct3,
  input  [6:0] funct7,
  output [2:0] ExtOp,
  output RegWr,
  output [2:0] BandJ,
  output ALUASrc,
  output [1:0] ALUBSrc,
  output [3:0] ALUctr,
  output MemtoReg,
  output [2:0] MemOp,
  output MemWr
);

  wire and_1_out, and_2_out, and_5_out, and_6_out, and_7_out, and_8_out, and_10_out, and_11_out, and_12_out,
       and_15_out, and_16_out, and_17_out, and_18_out, and_23_out, and_24_out, and_25_out, and_26_out,
       and_27_out, and_28_out, and_29_out, and_30_out;

  or or_1 (ExtOp[0], and_1_out, and_2_out);
  and and_1 (and_1_out, opcode[0], opcode[1], opcode[2], ~opcode[3], opcode[4], ~opcode[6]);  // AND_Gate
  and and_2 (and_2_out, opcode[0], opcode[1], ~opcode[2], ~opcode[3], ~opcode[4], opcode[5], opcode[6]);  // AND_Gate
  and and_3 (ExtOp[1], opcode[0], opcode[1], ~opcode[2], ~opcode[3], ~opcode[4], opcode[5]);  // AND_Gate
  and and_4 (ExtOp[2], opcode[0], opcode[1], opcode[2], opcode[3], ~opcode[4], opcode[5], opcode[6]);  // AND_Gate
  or or_2 (RegWr, and_5_out, and_6_out, and_7_out);
  and and_5 (and_5_out, opcode[0], opcode[1], ~opcode[3], opcode[4], ~opcode[6]);  // AND_Gate
  and and_6 (and_6_out, opcode[0], opcode[1], opcode[2], ~opcode[4], opcode[5], opcode[6]);  // AND_Gate
  and and_7 (and_7_out, opcode[0], opcode[1], ~opcode[2], ~opcode[3], ~opcode[4], ~opcode[5], ~opcode[6]);  // AND_Gate
  or or_3 (ALUASrc, and_8_out, ALUBSrc[0]);
  and and_8 (and_8_out, opcode[0], opcode[1], opcode[2], ~opcode[3], opcode[4], ~opcode[5], ~opcode[6]);  // AND_Gate
  and and_9 (ALUBSrc[0], opcode[0], opcode[1], opcode[2], ~opcode[4], opcode[5], opcode[6]);  // AND_Gate
  or or_4 (ALUBSrc[1], and_10_out, and_11_out, and_12_out);
  and and_10 (and_10_out, opcode[0], opcode[1], opcode[2], ~opcode[3], opcode[4], ~opcode[6]);  // AND_Gate
  and and_11 (and_11_out, opcode[0], opcode[1], ~opcode[2], ~opcode[3], opcode[4], ~opcode[5], ~opcode[6]);  // AND_Gate
  and and_12 (and_12_out, opcode[0], opcode[1], ~opcode[2], ~opcode[3], ~opcode[4], ~opcode[6]);  // AND_Gate
  and and_13 (MemtoReg, opcode[0], opcode[1], ~opcode[2], ~opcode[3], ~opcode[4], ~opcode[5], ~opcode[6]);  // AND_Gate
  and and_14 (MemWr, opcode[0], opcode[1], ~opcode[2], ~opcode[3], ~opcode[4], opcode[5], ~opcode[6]);  // AND_Gate
  and and_15 (and_15_out, opcode[0], opcode[1], opcode[2], opcode[3], ~opcode[4], opcode[5], opcode[6]);  // AND_Gate
  and and_16 (and_16_out, funct3[0], opcode[0], opcode[1], ~opcode[2], ~opcode[3], ~opcode[4], opcode[5], opcode[6]);  // AND_Gate
  and and_17 (and_17_out, ~funct3[0], ~funct3[1], ~funct3[2], opcode[0], opcode[1], opcode[2], ~opcode[3], ~opcode[4], opcode[5], opcode[6]);  // AND_Gate
  and and_18 (and_18_out, funct3[2], opcode[0], opcode[1], ~opcode[2], ~opcode[3], ~opcode[4], opcode[5], opcode[6]);  // AND_Gate
  and and_19 (BandJ[2], opcode[0], opcode[1], ~opcode[2], ~opcode[3], ~opcode[4], opcode[5], opcode[6]);  // AND_Gate
  and and_20 (MemOp[0], ~funct3[0], ~funct3[1], opcode[0], opcode[1], ~opcode[2], ~opcode[3], ~opcode[4], ~opcode[6]);  // AND_Gate
  and and_21 (MemOp[1], funct3[0], ~funct3[1], opcode[0], opcode[1], ~opcode[2], ~opcode[3], ~opcode[4], ~opcode[6]);  // AND_Gate
  and and_22 (MemOp[2], ~funct3[1], ~funct3[2], opcode[0], opcode[1], ~opcode[2], ~opcode[3], ~opcode[4], ~opcode[6]);  // AND_Gate
  or or_5 (BandJ[0], and_15_out, and_16_out);
  or or_6 (BandJ[1], and_17_out, and_18_out);
  or or_7 (ALUctr[0], and_23_out, and_24_out, and_30_out);
  and and_23 (and_23_out, funct3[0], opcode[0], opcode[1], ~opcode[3], opcode[4], ~opcode[6]);  // AND_Gate
  and and_24 (and_24_out, funct3[1], funct3[2], opcode[0], opcode[1], ~opcode[2], ~opcode[3], ~opcode[4], opcode[5], opcode[6]);  // AND_Gate
  or or_8 (ALUctr[1], and_25_out, and_26_out, and_30_out);
  and and_25 (and_25_out, funct3[1], opcode[0], opcode[1], ~opcode[3], opcode[4], ~opcode[6]);  // AND_Gate
  and and_26 (and_26_out, opcode[0], opcode[1], ~opcode[2], ~opcode[3], ~opcode[4], opcode[5], opcode[6]);  // AND_Gate
  or or_9 (ALUctr[2], and_27_out, and_30_out);
  and and_27 (and_27_out, funct3[2], opcode[0], opcode[1], ~opcode[3], opcode[4], ~opcode[6]);  // AND_Gate
  or or_10 (ALUctr[3], and_28_out, and_29_out, and_30_out);
  and and_28 (and_28_out, funct7[5], funct3[0], ~funct3[1], funct3[2], opcode[0], opcode[1], ~opcode[2], ~opcode[3], opcode[4], ~opcode[5], ~opcode[6]);  // AND_Gate
  and and_29 (and_29_out, funct7[5], opcode[0], opcode[1], ~opcode[2], ~opcode[3], opcode[4], opcode[5], ~opcode[6]);  // AND_Gate
  and and_30 (and_30_out, opcode[0], opcode[1], opcode[2], ~opcode[3], opcode[4], opcode[5], ~opcode[6]);  // AND_Gate

  // Notes on the sheet:
  //   输入引脚
  //   请勿修改引脚名称、电路名称及电路封装外观
  //   提示：根据指令种类，把7位指令code用一位指令类型标志位来表示，再通过功能码来区分具体指令，生成控制信号。
  //   输出引脚
endmodule
